# Fritzing sketch Light Rider_RPi_free (saved by Fritzing 0.8.5b)
stripboards: 1

parts:
  IC2 = ULN2003A [package="DIP16 [THT]"]
  Raspberry_Pi_B_rev1 = Raspberry Pi B rev2
  IC1 = ULN2003A [package="DIP16 [THT]"]
  S1 = Pushbutton [package="[THT]"]
  S2 = Pushbutton [package="[THT]"]
  R2 = Resistor [tolerance=±5% resistance=150 package=THT]
  R3 = Resistor [tolerance=±5% resistance=150 package=THT]
  R4 = Resistor [tolerance=±5% resistance=150 package=THT]
  R5 = Resistor [tolerance=±5% resistance=150 package=THT]
  R6 = Resistor [tolerance=±5% resistance=150 package=THT]
  R7 = Resistor [tolerance=±5% resistance=150 package=THT]
  R8 = Resistor [tolerance=±5% resistance=150 package=THT]
  R9 = Resistor [tolerance=±5% resistance=150 package=THT]
  R10 = Resistor [tolerance=±5% resistance=150 package=THT]
  R11 = Resistor [tolerance=±5% resistance=150 package=THT]
  R12 = Resistor [tolerance=±5% resistance=150 package=THT]
  R13 = Resistor [tolerance=±5% resistance=150 package=THT]
  R14 = Resistor [tolerance=±5% resistance=150 package=THT]
  R15 = Resistor [tolerance=±5% resistance=150 package=THT]
  R16 = Resistor [tolerance=±5% resistance=150 package=THT]
  R17 = Resistor [tolerance=±5% resistance=150 package=THT]
  On_Board_LED_1 = LED - 3mm [color="Orange (620nm)" package="3 mm [THT]"]
  Power_LED = LED - 3mm [color="Red (633nm)" package="3 mm [THT]"]
  On_Board_LED_3 = LED - 3mm [color="Yellow (595nm)" package="3 mm [THT]"]
  On_Board_LED_2 = LED - 3mm [color="Green (570nm)" package="3 mm [THT]"]
  R18 = Resistor [tolerance=±5% resistance=220 package=THT]
  R19 = Resistor [tolerance=±5% resistance=390 package=THT]
  J1 = male pin header, 3 pins [form="♂ (male)"]
  J2 = male pin header, 7 pins [form="♂ (male)"]
  LED_1 = LED - 5mm [color="White (4500K)" package="5 mm [THT]"]
  LED_2 = LED - 5mm [color="White (4500K)" package="5 mm [THT]"]
  LED_3 = LED - 5mm [color="White (4500K)" package="5 mm [THT]"]
  LED_4 = LED - 5mm [color="White (4500K)" package="5 mm [THT]"]
  LED_6 = LED - 5mm [color="White (4500K)" package="5 mm [THT]"]
  LED_5 = LED - 5mm [color="White (4500K)" package="5 mm [THT]"]
  LED_8 = LED - 5mm [color="White (4500K)" package="5 mm [THT]"]
  LED_7 = LED - 5mm [color="White (4500K)" package="5 mm [THT]"]
  LED_9 = LED - 5mm [color="White (4500K)" package="5 mm [THT]"]
  LED_10 = LED - 5mm [color="White (4500K)" package="5 mm [THT]"]
  LED_11 = LED - 5mm [color="White (4500K)" package="5 mm [THT]"]
  LED_12 = LED - 5mm [color="White (4500K)" package="5 mm [THT]"]
  J3 = male pin header, 7 pins [form="♂ (male)"]

nets:
  N1: IC2.In_1, Raspberry_Pi_B_rev1.GPIO_22
  N2: IC2.In_2, Raspberry_Pi_B_rev1.GPIO_23
  N3: IC2.In_3, Raspberry_Pi_B_rev1.GPIO_24
  N4: IC2.In_4, Raspberry_Pi_B_rev1.GPIO_10
  N5: IC2.In_5, Raspberry_Pi_B_rev1.GPIO_9
  N6: IC2.In_6, Raspberry_Pi_B_rev1.GPIO_25
  N7: IC2.In_7, Raspberry_Pi_B_rev1.GPIO_8
  N8: IC2.0V, Raspberry_Pi_B_rev1.GND, IC1.0V, S1.Pin_1, S1.Pin_2, S2.Pin_1, S2.Pin_2, R18.Pin_1, R19.Pin_0, J1.pin3
  N9: IC2.COM_-_Common, IC1.COM_-_Common, Power_LED.anode, On_Board_LED_3.anode, On_Board_LED_2.anode, J1.pin1, J2.pin1, LED_1.anode, LED_2.anode, LED_3.anode, LED_4.anode, LED_6.anode, LED_5.anode, LED_8.anode, LED_7.anode, LED_9.anode, LED_10.anode, LED_11.anode, LED_12.anode, J3.pin1
  N10: IC2.Out_7, R9.Pin_0
  N11: IC2.Out_6, R15.Pin_0
  N12: IC2.Out_5, R14.Pin_0
  N13: IC2.Out_4, R13.Pin_0
  N14: IC2.Out_3, R12.Pin_0
  N15: IC2.Out_2, R11.Pin_0
  N16: IC2.Out_1, R10.Pin_0
  N17: Raspberry_Pi_B_rev1.GPIO_2, S1.Pin_3, S1.Pin_4
  N18: Raspberry_Pi_B_rev1.GPIO_3, S2.Pin_3, S2.Pin_4
  N19: Raspberry_Pi_B_rev1.GPIO_14, IC1.In_2
  N20: Raspberry_Pi_B_rev1.GPIO_15, IC1.In_3
  N21: Raspberry_Pi_B_rev1.GPIO_17, IC1.In_4
  N22: Raspberry_Pi_B_rev1.GPIO_18, IC1.In_5
  N23: Raspberry_Pi_B_rev1.GPIO_27, IC1.In_6
  N24: Raspberry_Pi_B_rev1.GPIO_4, IC1.In_1
  N25: Raspberry_Pi_B_rev1.GPIO_11, IC1.In_7
  N26: Raspberry_Pi_B_rev1.GPIO_7, On_Board_LED_1.anode
  N27: IC1.Out_7, R5.Pin_0
  N28: IC1.Out_6, R4.Pin_0
  N29: IC1.Out_5, R8.Pin_0
  N30: IC1.Out_4, R6.Pin_0
  N31: IC1.Out_3, R7.Pin_0
  N32: IC1.Out_2, R3.Pin_0
  N33: IC1.Out_1, R2.Pin_0
  N34: R2.Pin_1, J2.pin7, LED_1.cathode
  N35: R3.Pin_1, J2.pin6, LED_2.cathode
  N36: R4.Pin_1, J2.pin2, LED_6.cathode
  N37: R5.Pin_1, R17.Pin_0
  N38: R6.Pin_1, J2.pin4, LED_4.cathode
  N39: R7.Pin_1, J2.pin5, LED_3.cathode
  N40: R8.Pin_1, J2.pin3, LED_5.cathode
  N41: R9.Pin_1, R16.Pin_0
  N42: R10.Pin_1, LED_7.cathode, J3.pin7
  N43: R11.Pin_1, LED_8.cathode, J3.pin6
  N44: R12.Pin_1, LED_9.cathode, J3.pin5
  N45: R13.Pin_1, LED_10.cathode, J3.pin4
  N46: R14.Pin_1, LED_11.cathode, J3.pin3
  N47: R15.Pin_1, LED_12.cathode, J3.pin2
  N48: R16.Pin_1, On_Board_LED_3.cathode
  N49: R17.Pin_1, On_Board_LED_2.cathode
  N50: On_Board_LED_1.cathode, R18.Pin_0
  N51: Power_LED.cathode, R19.Pin_1

notes:
  LightRider on Printer
  1 (Pin7)
  2 (Pin8)
  3 (Pin10)
  4 (Pin11)
  5 (Pin12)
  6 (Pin13)
  7 (Pin15)
  11 (Pin21)
  10 (Pin19)
  9 (Pin18)
  8 (Pin16)
  12 (Pin22)
  GPIO Buffer Board
  Raspberry Pi GPIO
  LightRider, LightRider circuit diagram,   1
  LightRider
  (Rev.1)
